# Fritzing sketch iot_button_wemos (saved by Fritzing 0.9.3b)
circuit board: 5.23177cm x 2.93254cm

parts:
  U3 = LIPO-1000mAh [package=lipo-1000]
  S1 = Pushbutton [package="[SMD]"]
  WeMos_D1_Mini1 = WeMos D1 Mini

nets:
  N1: U3.+, WeMos_D1_Mini1.5V
  N2: U3.-, WeMos_D1_Mini1.G
  N3: S1.Pin_1, S1.Pin_2, WeMos_D1_Mini1.D8
  N4: S1.Pin_3, S1.Pin_4, WeMos_D1_Mini1.3V3
